# Fritzing sketch Skybot (saved by Fritzing 0.9.0b)
breadboards: 1

parts:
  Parte1 = Arduino Uno (Rev3)
  Parte2 = SRF05 Ultrasonic Rangefinder
  Parte3 = SRF05 Ultrasonic Rangefinder
  J1 = Basic Servo
  J2 = Basic Servo

nets:
  N1: Parte1.A3, Parte2.Echo
  N2: Parte1.A4/SDA, Parte3.Echo
  N3: Parte1.D12/MISO, J1.pulse
  GND: Parte1.GND, Parte2.GND, Parte3.GND, J1.gnd, J2.gnd
  N4: Parte1.D3_PWM, Parte2.Trig
  N5: Parte1.D4, Parte3.Trig
  N6: Parte1.D6_PWM, J2.pulse
  VCC: Parte1.5V, Parte2.VCC, Parte3.VCC, J1.vcc, J2.vcc

notes:
  5V
  GND
  Derecha / Eskubia
  Izquierda / Ezkerra
